// Logisim project OluwapelumiAdewuyi_PasswordChecker.circ as structural Verilog: 1 circuit, main circuit main
module main (
  input  A,
  input  B,
  input  C,
  output Unlocked
);

  not not_1 (B, B);
  and and_1 (Unlocked, B, B, B);

  assign C = B;
endmodule
